# Fritzing sketch johnny-ruxpin (saved by Fritzing 0.9.4)
breadboards: 1

parts:
  Part1 = Motor Driver 1A Dual TB6612FNG  # not connected
  Raspberry_Pi_1 = Raspberry Pi 3 [part_number=RPI-3-V1.2]
  M1 = DC Motor  # not connected
  VCC1 = Battery
  M2 = DC Motor  # not connected

nets:
  3V3: Raspberry_Pi_1.3v3, Raspberry_Pi_1.GPIO2, Raspberry_Pi_1.GPIO3, Raspberry_Pi_1.GPIO27, Raspberry_Pi_1.GPIO22, Raspberry_Pi_1.3V3
  N1: Raspberry_Pi_1.GND, VCC1.-
  N2: Raspberry_Pi_1.GPIO24, Raspberry_Pi_1.GPIO23
  N3: Raspberry_Pi_1.GPIO18, Raspberry_Pi_1.GPIO15
